# Fritzing sketch ardu-pi (saved by Fritzing 0.9.3b)

parts:
  Raspberry_Pi_1 = Raspberry Pi 3 [part_number=RPI-3-V1.2]  # not connected
  Part1 = Arduino Uno (Rev3)
  Raspberry_Pi_Sense_Hat1 = Raspberry Pi Sense Hat  # not connected
  M1 = DC Motor
  D1 = SOLAR-IXYS [package=solarbit-12x1]

nets:
  N1: Part1.A0, M1.pin_1
  N2: Part1.A1, D1.C
  N3: Part1.GND, M1.pin_2, D1.A

custom parts:
  Raspberry Pi Sense Hat: The Sense HAT is an add-on board for Raspberry Pi, made especially for the Astro Pi mission – it launched to the International Space Station in December 2015. The Sense HAT has an 8×8 RGB LED matrix, a five-button joystick and includes the following sensors: Gyroscope Accelerometer Magnetometer Temperature Barometric pressure Humidity
